// Logisim project cpu_main_circuit.circ as structural Verilog: 36 circuits, main circuit main
module main (
  input  RESET
);

  wire CLK_out, cu_with_rom_1_d0, cu_with_rom_1_d2, cu_with_rom_1_d3, cu_with_rom_1_d4, cu_with_rom_1_d5,
       cu_with_rom_1_d6, cu_with_rom_1_d7, cu_with_rom_1_d8, cu_with_rom_1_d9, cu_with_rom_1_d10,
       cu_with_rom_1_d11, cu_with_rom_1_d12, cu_with_rom_1_d13, display_driver_1_error,
       display_driver_1_sign_bit, flag_generator_1_arith_overflow, flag_generator_1_equal_flg,
       flag_generator_1_lsb_0_flg, flag_generator_1_neg_less, flag_generator_1_zero_flg,
       ins_decoder_1_halt_opcode, jump_logic_1_jump, or_1_out;
  wire [2:0] alu_and_mux_1_comparisn, cu_with_rom_1_d14_15, ins_decoder_1_alu_op, ins_decoder_1_dest_res,
       ins_decoder_1_src_b;
  wire [3:0] display_driver_1_display_pins, display_driver_1_display_pins_2;
  wire [4:0] flg_resister_1_flg_o0, ins_decoder_1_opcode;
  wire [7:0] A_B_BUFFER_out_r0, A_B_BUFFER_out_r1, ACCUMULATOR_q, alu_and_mux_1_alu_out, ins_decoder_1_data,
       ins_decoder_1_jump_address, multiplexer_1_out, multiplexer_2_out, muxed_gp_res_1_data_out,
       program_counter_1_current_addr;
  wire [11:8] display_driver_1_display_pins_3;
  wire [15:0] INS_RES_q, PROGRAM_MEMORY_data;

  PROGRAM_COUNTER program_counter_1 (
    .JMP_ADDR(ins_decoder_1_jump_address), .HALT(ins_decoder_1_halt_opcode), .JUMP_OTHERS(jump_logic_1_jump),
    .WE_PC(cu_with_rom_1_d12), .CLK(CLK_out), .RESET(RESET), .CURRENT_ADDR(program_counter_1_current_addr));
  Clock CLK (.out(CLK_out));
  ROM #(.dataWidth(16)) PROGRAM_MEMORY (.addr(program_counter_1_current_addr), .data(PROGRAM_MEMORY_data));
  JUMP_LOGIC jump_logic_1 (
    .jump_logic_sel(cu_with_rom_1_d14_15), .t(cu_with_rom_1_d13), .jump_flgs(flg_resister_1_flg_o0),
    .jump(jump_logic_1_jump));
  Register #(.width(16)) INS_RES (
    .D(PROGRAM_MEMORY_data), .en(cu_with_rom_1_d11), .clk(CLK_out), .Q(INS_RES_q), .clr(RESET));
  INS_DECODER ins_decoder_1 (
    .INSTRUCTION_INP(INS_RES_q), .JUMP_ADDRESS(ins_decoder_1_jump_address), .DATA(ins_decoder_1_data),
    .OPCODE(ins_decoder_1_opcode), .SRC_B(ins_decoder_1_src_b), .DEST_RES(ins_decoder_1_dest_res),
    .ALU_OP(ins_decoder_1_alu_op), .HALT_OPCODE(ins_decoder_1_halt_opcode));
  or or_1 (or_1_out, RESET, cu_with_rom_1_d0);
  Register ACCUMULATOR (.D(multiplexer_1_out), .en(cu_with_rom_1_d9), .clk(CLK_out), .Q(ACCUMULATOR_q), .clr(RESET));
  Multiplexer #(.width(8)) multiplexer_1 (
    .in0(multiplexer_2_out), .in1(ins_decoder_1_data), .out(multiplexer_1_out), .sel(cu_with_rom_1_d6));
  CU_WITH_ROM cu_with_rom_1 (
    .ENB_CNTR(cu_with_rom_1_d2), .COUNTER_RESET(or_1_out), .CLK(CLK_out), .OPCODE(ins_decoder_1_opcode),
    .D0(cu_with_rom_1_d0), .D1(cu_with_rom_1_d14_15[2]), .D2(cu_with_rom_1_d2), .D3(cu_with_rom_1_d3),
    .D4(cu_with_rom_1_d4), .D5(cu_with_rom_1_d5), .D6(cu_with_rom_1_d6), .D7(cu_with_rom_1_d7),
    .D8(cu_with_rom_1_d8), .D9(cu_with_rom_1_d9), .D10(cu_with_rom_1_d10), .D11(cu_with_rom_1_d11),
    .D12(cu_with_rom_1_d12), .D13(cu_with_rom_1_d13), .D14_15(cu_with_rom_1_d14_15[1:0]));
  MUXED_GP_RES muxed_gp_res_1 (
    .WE_T(cu_with_rom_1_d8), .CLEAR_ALL(RESET), .CLK(CLK_out), .WE_SEL(ins_decoder_1_dest_res),
    .DATA_IN(ACCUMULATOR_q), .SEL_RES(ins_decoder_1_src_b), .DATA_OUT(muxed_gp_res_1_data_out));
  DISPLAY_DRIVER display_driver_1 (
    .DATA_IN(muxed_gp_res_1_data_out), .OVERFLOW(flg_resister_1_flg_o0[1]), .PRINT_ENB(cu_with_rom_1_d10),
    .RST(RESET),
    .DISPLAY_PINS({display_driver_1_display_pins_3, display_driver_1_display_pins_2, display_driver_1_display_pins}),
    .SIGN_BIT(display_driver_1_sign_bit), .ERROR(display_driver_1_error));
  AB_BUFFER A_B_BUFFER (
    .WE_A(cu_with_rom_1_d4), .WE_B(cu_with_rom_1_d3), .CLR(RESET), .CLK(CLK_out), .IN_R0(ACCUMULATOR_q),
    .IN_R1(muxed_gp_res_1_data_out), .OUT_R0(A_B_BUFFER_out_r0), .OUT_R1(A_B_BUFFER_out_r1));
  _7_Segment_Display SIGN (
    .g(display_driver_1_sign_bit), .f(display_driver_1_error), .a(display_driver_1_error),
    .e(display_driver_1_error), .d(display_driver_1_error));  // open: b, c, dp
  ALU_AND_MUX alu_and_mux_1 (
    .A(A_B_BUFFER_out_r0), .S(ins_decoder_1_alu_op), .B(A_B_BUFFER_out_r1),
    .COMPARISN(alu_and_mux_1_comparisn), .ALU_OUT(alu_and_mux_1_alu_out));  // open: CARRY
  Hex_Digit_Display DIGIT_2 (.value(display_driver_1_display_pins_2));  // open: dp
  Hex_Digit_Display DIGIT_3 (.value(display_driver_1_display_pins_3));  // open: dp
  Multiplexer #(.width(8)) multiplexer_2 (
    .in0(alu_and_mux_1_alu_out), .in1(A_B_BUFFER_out_r1), .out(multiplexer_2_out), .sel(cu_with_rom_1_d5));
  FLAG_GENERATOR flag_generator_1 (
    .A7_IN(A_B_BUFFER_out_r0[7]), .B7_IN(A_B_BUFFER_out_r1[7]), .COMPARATOR_IN(alu_and_mux_1_comparisn),
    .RESULT_IN(multiplexer_2_out), .ARITH_OVERFLOW(flag_generator_1_arith_overflow),
    .LSB_0_FLG(flag_generator_1_lsb_0_flg), .ZERO_FLG(flag_generator_1_zero_flg),
    .NEG_LESS(flag_generator_1_neg_less), .EQUAL_FLG(flag_generator_1_equal_flg));
  Hex_Digit_Display DIGIT_1 (.value(display_driver_1_display_pins));  // open: dp
  FLG_RESISTER flg_resister_1 (
    .WE_FLG(cu_with_rom_1_d7), .CLK(CLK_out), .CLR_FLG(RESET), .FLG_0(flag_generator_1_zero_flg),
    .FLG_1(flag_generator_1_neg_less), .FLG_2(flag_generator_1_arith_overflow),
    .FLG_3(flag_generator_1_equal_flg), .FLG_4(flag_generator_1_lsb_0_flg),
    .FLG_O0(flg_resister_1_flg_o0[0]), .FLG_O1(flg_resister_1_flg_o0[1]), .FLG_O2(flg_resister_1_flg_o0[2]),
    .FLG_O3(flg_resister_1_flg_o0[3]), .FLG_O4(flg_resister_1_flg_o0[4]));

  // Notes on the sheet:
  //   contents of PROGRAM_MEMORY (hex, n*v repeats v):
  //   15 900 15 1400 5 800 5040 4037 5000 4037 4828 1040 1020 a00 1005 800 6008 23*0 1040 1400 1005 800
  //   6008 10*0 1840 f800
  //   JUMP_ADDRESS_PATH
  //   FEEDBACK_PATH
endmodule

module FULL_ADDER (
  input  Cin,
  input  A,
  input  B,
  output S,
  output Cout
);

  wire and_1_out, and_2_out, xor_1_out;

  xor xor_1 (xor_1_out, A, B);
  and and_1 (and_1_out, B, A);
  xor xor_2 (S, Cin, xor_1_out);
  and and_2 (and_2_out, xor_1_out, Cin);
  or or_1 (Cout, and_2_out, and_1_out);
endmodule

// ADR_SUBST
module ADD_SUBS (
  input  M,
  input  [7:0] B,
  input  [7:0] A,
  output [7:0] S,
  output Cout
);

  wire full_adder_1_cout, full_adder_2_cout, full_adder_3_cout, full_adder_4_cout, full_adder_5_cout,
       full_adder_6_cout, full_adder_7_cout, xor_1_out, xor_2_out, xor_3_out, xor_4_out, xor_5_out,
       xor_6_out, xor_7_out, xor_8_out;

  xor xor_1 (xor_1_out, M, B[0]);
  FULL_ADDER full_adder_1 (.Cin(M), .A(A[0]), .B(xor_1_out), .S(S[0]), .Cout(full_adder_1_cout));
  xor xor_2 (xor_2_out, M, B[1]);
  FULL_ADDER full_adder_2 (.Cin(full_adder_1_cout), .A(A[1]), .B(xor_2_out), .S(S[1]), .Cout(full_adder_2_cout));
  xor xor_3 (xor_3_out, M, B[2]);
  FULL_ADDER full_adder_3 (.Cin(full_adder_2_cout), .A(A[2]), .B(xor_3_out), .S(S[2]), .Cout(full_adder_3_cout));
  xor xor_4 (xor_4_out, M, B[3]);
  FULL_ADDER full_adder_4 (.Cin(full_adder_3_cout), .A(A[3]), .B(xor_4_out), .S(S[3]), .Cout(full_adder_4_cout));
  FULL_ADDER full_adder_5 (.Cin(full_adder_4_cout), .A(A[4]), .B(xor_5_out), .S(S[4]), .Cout(full_adder_5_cout));
  xor xor_5 (xor_5_out, M, B[4]);
  FULL_ADDER full_adder_6 (.Cin(full_adder_5_cout), .A(A[5]), .B(xor_6_out), .S(S[5]), .Cout(full_adder_6_cout));
  xor xor_6 (xor_6_out, M, B[5]);
  FULL_ADDER full_adder_7 (.Cin(full_adder_6_cout), .A(A[6]), .B(xor_7_out), .S(S[6]), .Cout(full_adder_7_cout));
  xor xor_7 (xor_7_out, M, B[6]);
  FULL_ADDER full_adder_8 (.Cin(full_adder_7_cout), .A(A[7]), .B(xor_8_out), .S(S[7]), .Cout(Cout));
  xor xor_8 (xor_8_out, M, B[7]);
endmodule

// DCDR_4X2
module DEC_4X2 (
  input  I3,
  input  I2,
  input  I1,
  input  I0,
  input  [1:0] S,
  output Y
);

  wire and_1_out, and_2_out, and_3_out, and_4_out, not_1_out, not_2_out;

  not not_1 (not_1_out, S[1]);
  and and_1 (and_1_out, I3, S[1], S[0]);
  and and_2 (and_2_out, I2, S[1], not_2_out);
  and and_3 (and_3_out, I1, S[0], not_1_out);
  and and_4 (and_4_out, I0, not_1_out, not_2_out);
  not not_2 (not_2_out, S[0]);
  or or_1 (Y, and_1_out, and_2_out, and_3_out, and_4_out);
endmodule

module DEC_8BIT_4X2 (
  input  [1:0] S0,
  input  [7:0] I_0,
  input  [7:0] I_1,
  input  [7:0] I_2,
  input  [7:0] I_3,
  output [7:0] Y
);

  DEC_4X2 dec_4x2_1 (.I3(I_3[7]), .I2(I_2[7]), .I1(I_1[7]), .I0(I_0[7]), .S(S0), .Y(Y[7]));
  DEC_4X2 dec_4x2_2 (.I3(I_3[6]), .I2(I_2[6]), .I1(I_1[6]), .I0(I_0[6]), .S(S0), .Y(Y[6]));
  DEC_4X2 dec_4x2_3 (.I3(I_3[5]), .I2(I_2[5]), .I1(I_1[5]), .I0(I_0[5]), .S(S0), .Y(Y[5]));
  DEC_4X2 dec_4x2_4 (.I3(I_3[4]), .I2(I_2[4]), .I1(I_1[4]), .I0(I_0[4]), .S(S0), .Y(Y[4]));
  DEC_4X2 dec_4x2_5 (.I3(I_3[3]), .I2(I_2[3]), .I1(I_1[3]), .I0(I_0[3]), .S(S0), .Y(Y[3]));
  DEC_4X2 dec_4x2_6 (.I3(I_3[2]), .I2(I_2[2]), .I1(I_1[2]), .I0(I_0[2]), .S(S0), .Y(Y[2]));
  DEC_4X2 dec_4x2_7 (.I3(I_3[1]), .I2(I_2[1]), .I1(I_1[1]), .I0(I_0[1]), .S(S0), .Y(Y[1]));
  DEC_4X2 dec_4x2_8 (.I3(I_3[0]), .I2(I_2[0]), .I1(I_1[0]), .I0(I_0[0]), .S(S0), .Y(Y[0]));
endmodule

module OR_1BIT (
  input  in_1,
  input  in_2,
  output out_3
);

  or or_1 (out_3, in_1, in_2);
endmodule

module OR_8BIT (
  input  [7:0] A,
  input  [7:0] B,
  output [7:0] Y
);

  or or_1 (Y[0], A[0], B[0]);
  or or_2 (Y[1], A[1], B[1]);
  or or_3 (Y[2], A[2], B[2]);
  or or_4 (Y[3], A[3], B[3]);
  or or_5 (Y[4], A[4], B[4]);
  or or_6 (Y[5], A[5], B[5]);
  or or_7 (Y[6], A[6], B[6]);
  or or_8 (Y[7], A[7], B[7]);
endmodule

module AND_1BIT (
  input  in_1,
  input  in_2,
  output out_3
);

  and and_1 (out_3, in_1, in_2);
endmodule

module AND_8BIT (
  input  [7:0] A,
  input  [7:0] B,
  output [7:0] Y
);

  and and_1 (Y[0], A[0], B[0]);
  and and_2 (Y[1], A[1], B[1]);
  and and_3 (Y[2], A[2], B[2]);
  and and_4 (Y[3], A[3], B[3]);
  and and_5 (Y[4], A[4], B[4]);
  and and_6 (Y[5], A[5], B[5]);
  and and_7 (Y[6], A[6], B[6]);
  and and_8 (Y[7], A[7], B[7]);
endmodule

module TEST (
  input  B7,
  input  A7,
  input  B6,
  input  A6,
  input  B5,
  input  A5,
  input  B4,
  input  A4,
  input  B3,
  input  A3,
  input  B2,
  input  A2,
  input  in_13,
  input  B1,
  input  A1,
  input  B0,
  input  A0,
  input  A,
  input  B,
  input  in_20,
  input  in_21,
  input  [7:0] in_22,
  output S7,
  output S6,
  output S5,
  output S4,
  output S3,
  output S2,
  output S1,
  output S0,
  output out_31,
  output out_32,
  output [15:0] ir_data
);

  wire AND_1_out_3, F_ADDER_s, full_adder_1_cout, full_adder_2_cout, full_adder_3_cout, full_adder_4_cout,
       full_adder_5_cout, full_adder_6_cout, full_adder_7_cout, OR_1_p4, xor_1_out, xor_2_out, xor_3_out,
       xor_4_out, xor_5_out, xor_6_out, xor_7_out, xor_8_out;
  wire [9:0] mar_q;
  wire [15:0] ram_1_dout;

  Register #(.width(10)) mar (.Q(mar_q));  // open: D, en, clk, clr
  FULL_ADDER full_adder_1 (.Cin(in_13), .A(A7), .B(xor_1_out), .S(S0), .Cout(full_adder_1_cout));
  xor xor_1 (xor_1_out, in_13, B7);
  xor xor_2 (xor_2_out, in_13, B6);
  RAM #(.addrWidth(10), .dataWidth(16)) ram_1 (.addr(mar_q), .dout(ram_1_dout));  // open: we, oe, clk, din
  FULL_ADDER full_adder_2 (.Cin(full_adder_1_cout), .A(A6), .B(xor_2_out), .S(S1), .Cout(full_adder_2_cout));
  xor xor_3 (xor_3_out, in_13, B5);
  ROM #(.addrWidth(7), .dataWidth(4)) rom_1 ();  // open: addr, data
  ROM #(.addrWidth(7), .dataWidth(4)) rom_2 ();  // open: addr, data
  FULL_ADDER full_adder_3 (.Cin(full_adder_2_cout), .A(A5), .B(xor_3_out), .S(S2), .Cout(full_adder_3_cout));
  xor xor_4 (xor_4_out, in_13, B4);
  FULL_ADDER full_adder_4 (.Cin(full_adder_3_cout), .A(A4), .B(xor_4_out), .S(S3), .Cout(full_adder_4_cout));
  xor xor_5 (xor_5_out, in_13, B3);
  FULL_ADDER F_ADDER (.A(A), .B(B), .S(F_ADDER_s));  // open: Cin, Cout
  // OR_1BIT OR_1: pin names not known; wires that end beside it: A, B, A, OR_1_p4
  AND_1BIT AND_1 (.in_1(A), .in_2(B), .out_3(AND_1_out_3));
  Register #(.width(16)) mbr (.D(ram_1_dout), .Q(ir_data));  // open: en, clk, clr
  FULL_ADDER full_adder_5 (.Cin(full_adder_4_cout), .A(A3), .B(xor_5_out), .S(S4), .Cout(full_adder_5_cout));
  // DEC_4X2 MUX_4X2: pin names not known; wires that end beside it: F_ADDER_s, OR_1_p4, AND_1_out_3, in_21, in_20, out_32
  FULL_ADDER full_adder_6 (.Cin(full_adder_5_cout), .A(A2), .B(xor_6_out), .S(S5), .Cout(full_adder_6_cout));
  xor xor_6 (xor_6_out, in_13, B2);
  FULL_ADDER full_adder_7 (.Cin(full_adder_6_cout), .A(A1), .B(xor_7_out), .S(S6), .Cout(full_adder_7_cout));
  xor xor_7 (xor_7_out, in_13, B1);
  FULL_ADDER full_adder_8 (.Cin(full_adder_7_cout), .A(A0), .B(xor_8_out), .S(S7), .Cout(out_31));
  xor xor_8 (xor_8_out, in_13, B0);

  // Notes on the sheet:
  //   contents of rom_1 (hex, n*v repeats v):
  //   10*0 10*1 10*2 10*3 10*4 10*5
  //   contents of rom_2 (hex, n*v repeats v):
  //   0 1 2 3 4 5 6 7 8 9 0 1 2 3 4 5 6 7 8 9 0 1 2 3 4 5 6 7 8 9 0 1
endmodule

// ALU_WT_MUX
module ALU_AND_MUX (
  input  [7:0] A,
  input  [7:0] B,
  input  [2:0] S,
  output CARRY,
  output [7:0] ALU_OUT,
  output [2:0] COMPARISN
);

  wire add_subs_1_cout, add_subs_2_cout, not_1_out;
  wire [7:0] add_subs_1_s, add_subs_2_s, and_1_out, or_1_out, shifter_1_out, shifter_2_out, shifter_3_out;

  assign or_1_out = A | B;  // OR_Gate or_1, 8 bits wide
  assign and_1_out = A & B;  // AND_Gate and_1, 8 bits wide
  ADD_SUBS add_subs_1 (.A(A), .B(B), .S(add_subs_1_s), .Cout(add_subs_1_cout));  // open: M
  not not_1 (not_1_out, add_subs_2_cout);
  ADD_SUBS add_subs_2 (.A(A), .M(1'b1), .B(B), .S(add_subs_2_s), .Cout(add_subs_2_cout));
  Shifter shifter_1 (.in(B), .\dist (3'b001), .out(shifter_1_out));
  Shifter #(.shift("ar")) shifter_2 (.in(B), .\dist (3'b001), .out(shifter_2_out));
  Shifter #(.shift("rr")) shifter_3 (.in(B), .\dist (3'b001), .out(shifter_3_out));
  Comparator comparator_1 (.a(A), .b(B), .gt(COMPARISN[0]), .eq(COMPARISN[1]), .lt(COMPARISN[2]));
  or or_2 (CARRY, add_subs_1_cout, not_1_out);
  Multiplexer #(.select(3), .width(8)) multiplexer_1 (
    .in0(add_subs_1_s), .in1(add_subs_2_s), .in2(or_1_out), .in3(and_1_out), .in4(shifter_1_out),
    .in5(shifter_2_out), .in6(shifter_3_out), .in7({8{1'b0}}), .out(ALU_OUT), .sel(S));
endmodule

// GP_RESISTER
module GP_RES (
  input  [7:0] IN_RES,
  input  WE_T,
  input  [2:0] WE_SEL,
  input  CLR_SEL,
  input  CLK,
  output [7:0] OUT_R0,
  output [7:0] OUT_R1,
  output [7:0] OUT_R2,
  output [7:0] OUT_R3,
  output [7:0] OUT_R4,
  output [7:0] OUT_R5,
  output [7:0] OUT_R6,
  output [7:0] OUT_R7
);

  wire [7:0] gp_resister_mux_1_we_selected_resister;

  GP_RESISTER_MUX gp_resister_mux_1 (
    .WE_T(WE_T), .WE_SEL(WE_SEL), .WE_SELECTED_RESISTER(gp_resister_mux_1_we_selected_resister));
  Register register_1 (
    .D(IN_RES), .en(gp_resister_mux_1_we_selected_resister[0]), .clk(CLK), .Q(OUT_R0), .clr(CLR_SEL));
  Register register_2 (
    .D(IN_RES), .en(gp_resister_mux_1_we_selected_resister[1]), .clk(CLK), .Q(OUT_R1), .clr(CLR_SEL));
  Register register_3 (
    .D(IN_RES), .en(gp_resister_mux_1_we_selected_resister[2]), .clk(CLK), .Q(OUT_R2), .clr(CLR_SEL));
  Register register_4 (
    .D(IN_RES), .en(gp_resister_mux_1_we_selected_resister[3]), .clk(CLK), .Q(OUT_R3), .clr(CLR_SEL));
  Register register_5 (
    .D(IN_RES), .en(gp_resister_mux_1_we_selected_resister[4]), .clk(CLK), .Q(OUT_R4), .clr(CLR_SEL));
  Register register_6 (
    .D(IN_RES), .en(gp_resister_mux_1_we_selected_resister[5]), .clk(CLK), .Q(OUT_R5), .clr(CLR_SEL));
  Register register_7 (
    .D(IN_RES), .en(gp_resister_mux_1_we_selected_resister[6]), .clk(CLK), .Q(OUT_R6), .clr(CLR_SEL));
  Register register_8 (
    .D(IN_RES), .en(gp_resister_mux_1_we_selected_resister[7]), .clk(CLK), .Q(OUT_R7), .clr(CLR_SEL));
endmodule

module SP_RES (
  input  [7:0] IN_R0,
  input  WE_R0,
  input  R0_CLR,
  input  [7:0] IN_R1,
  input  WE_R1,
  input  R1_CLR,
  input  [7:0] IN_R2,
  input  WE_R2,
  input  R2_CLR,
  input  CLK,
  output [7:0] OUT_R0,
  output [7:0] OUT_R1,
  output [7:0] OUT_R2
);

  Register register_1 (.D(IN_R0), .en(WE_R0), .clk(CLK), .Q(OUT_R0), .clr(R0_CLR));
  Register register_2 (.D(IN_R1), .en(WE_R1), .clk(CLK), .Q(OUT_R1), .clr(R1_CLR));
  Register register_3 (.D(IN_R2), .en(WE_R2), .clk(CLK), .Q(OUT_R2), .clr(R2_CLR));
endmodule

module TME_GEN (
  input  LD,
  input  [2:0] DATA,
  input  ENB,
  input  CLK,
  output [7:0] T
);

  wire and_1_out, not_1_out, not_2_out;
  wire [2:0] counter_1_q;

  Counter #(.max('h7), .width(3)) counter_1 (
    .load(LD), .D(DATA), .count(ENB), .Q(counter_1_q), .clk(CLK), .clr(and_1_out));  // open: carry, up
  and and_1 (and_1_out, not_1_out, not_2_out, counter_1_q[2]);
  not not_1 (not_1_out, counter_1_q[0]);
  not not_2 (not_2_out, counter_1_q[1]);
  Decoder #(.enable("false"), .select(3)) decoder_1 (
    .out0(T[0]), .out1(T[1]), .out2(T[2]), .out3(T[3]), .out4(T[4]), .out5(T[5]), .out6(T[6]), .out7(T[7]),
    .sel(counter_1_q));
endmodule

module CTRL_AND (
  input  T,
  input  INIT_MODE,
  output OP
);

  wire not_1_out;

  not not_1 (not_1_out, INIT_MODE);
  and and_1 (OP, T, not_1_out);
endmodule

// A_ND_B_BUFR
module AB_BUFFER (
  input  [7:0] IN_R0,
  input  WE_A,
  input  [7:0] IN_R1,
  input  WE_B,
  input  CLR,
  input  CLK,
  output [7:0] OUT_R0,
  output [7:0] OUT_R1
);

  Register register_1 (.D(IN_R0), .en(WE_A), .clk(CLK), .Q(OUT_R0));  // open: clr
  Register register_2 (.D(IN_R1), .en(WE_B), .clk(CLK), .Q(OUT_R1), .clr(CLR));
endmodule

module CU (
  input  [7:0] INSTRUCTION_IN,
  input  WE_INSTRUCTION,
  input  IR_RESET,
  input  INIT_MODE,
  input  CLK,
  output [1:0] SELECT_A,
  output [1:0] SELECT_B,
  output [1:0] WE_SEL,
  output T0,
  output T1,
  output ALU_MD,
  output T2,
  output MOV_MD,
  output T3,
  output CLR_MD,
  output RESERVED_MD
);

  wire not_1_out, or_1_out;
  wire [7:4] COUNTER_t;
  wire [7:6] IR_q;

  not not_1 (not_1_out, WE_INSTRUCTION);
  or or_1 (or_1_out, INIT_MODE, not_1_out);
  Register IR (
    .D(INSTRUCTION_IN), .en(WE_INSTRUCTION), .clk(CLK), .Q({IR_q, WE_SEL, SELECT_B, SELECT_A}), .clr(IR_RESET));
  TME_GEN COUNTER (.LD(INIT_MODE), .ENB(or_1_out), .CLK(CLK), .DATA(3'b011), .T({COUNTER_t, T3, T2, T1, T0}));
  Decoder #(.enable("false"), .select(2)) decoder_1 (
    .out0(ALU_MD), .out1(MOV_MD), .out2(CLR_MD), .out3(RESERVED_MD), .sel(IR_q));

  // Notes on the sheet:
  //   OPCODE
endmodule

module TESING_UNT (
  input  [2:0] MAN_DATA_TO_COUNTER,
  input  LOAD_MAN_DATA_TO_COUNTER,
  input  [15:0] in_3,
  input  in_4,
  input  [2:0] in_5,
  input  LD,
  input  [2:0] DATA,
  input  ENB,
  input  CLK,
  input  ENB_CNTR,
  output T4,
  output T5,
  output [3:0] INS_OUT,
  output T6,
  output [2:0] ALU_OP,
  output T7,
  output [7:0] out_17,
  output [2:0] RESERVED,
  output [2:0] SRC_B,
  output [2:0] SEL_RES_B,
  output [2:0] SEL_RES_A,
  output [2:0] DEST_RES_SEL,
  output [2:0] DEST_RES,
  output [7:0] DATA_OUT,
  output T0,
  output T1,
  output [4:0] OPCODE,
  output T2,
  output T3,
  output out_30,
  output out_31,
  output out_32,
  output out_33
);

  wire [1:0] undriven;
  wire [2:0] counter_1_q, undriven_2;

  Demultiplexer #(.select(2)) demultiplexer_1 (
    .out0(INS_OUT[0]), .out1(INS_OUT[1]), .out2(INS_OUT[2]), .out3(INS_OUT[3]), .sel(undriven));  // open: in
  Counter #(.max('h7), .width(3)) counter_1 (
    .load(LD), .D(DATA), .count(ENB), .Q(counter_1_q), .clk(CLK));  // open: carry, up, clr
  Decoder #(.enable("false"), .select(3)) decoder_1 (
    .out0(T0), .out1(T1), .out2(T2), .out3(T3), .out4(out_30), .out5(out_31), .out6(out_32), .out7(out_33),
    .sel(undriven_2));
  ROM rom_1 (.addr({1'b0, in_3[15:12], counter_1_q}), .data(DATA_OUT));

  assign DEST_RES_SEL = in_3[11:9];
  assign RESERVED = in_3[2:0];
  assign SEL_RES_A = in_3[8:6];
  assign SEL_RES_B = in_3[5:3];

  // Notes on the sheet:
  //   SEL_A
  //   SEL_A
  //   RES_SEL
  //   ALU
  //   SEL_A
  //   SEL_A
  //   RES_SEL
  //   ALU
endmodule

// GP_RES_MUX
module B_RESISTER_SELECTOR (
  input  [7:0] R0,
  input  [7:0] R1,
  input  [7:0] R2,
  input  [7:0] R3,
  input  [7:0] R4,
  input  [7:0] R5,
  input  [7:0] R6,
  input  [7:0] R7,
  input  [2:0] SEL_B,
  output [7:0] SELECTED_B
);

  Multiplexer #(.select(3), .width(8)) multiplexer_1 (
    .in0(R0), .in1(R1), .in2(R2), .in3(R3), .in4(R4), .in5(R5), .in6(R6), .in7(R7), .out(SELECTED_B),
    .sel(SEL_B));
endmodule

module GP_RESISTER_MUX (
  input  WE_T,
  input  [2:0] WE_SEL,
  output [7:0] WE_SELECTED_RESISTER
);

  Demultiplexer #(.select(3)) demultiplexer_1 (
    .out0(WE_SELECTED_RESISTER[0]), .out1(WE_SELECTED_RESISTER[1]), .out2(WE_SELECTED_RESISTER[2]),
    .out3(WE_SELECTED_RESISTER[3]), .out4(WE_SELECTED_RESISTER[4]), .out5(WE_SELECTED_RESISTER[5]),
    .out6(WE_SELECTED_RESISTER[6]), .out7(WE_SELECTED_RESISTER[7]), .in(WE_T), .sel(WE_SEL));
endmodule

// CONTROL_UNIT
module CU_WITH_ROM (
  input  [4:0] OPCODE,
  input  ENB_CNTR,
  input  COUNTER_RESET,
  input  CLK,
  output D0,
  output D1,
  output D2,
  output D3,
  output D4,
  output D5,
  output D6,
  output D7,
  output D8,
  output D9,
  output D10,
  output D11,
  output D12,
  output D13,
  output [1:0] D14_15
);

  wire [3:0] counter_4bit_1_cnt_out;

  ROM #(.addrWidth(9), .dataWidth(16)) rom_1 (
    .addr({OPCODE, counter_4bit_1_cnt_out}),
    .data({D14_15, D13, D12, D11, D10, D9, D8, D7, D6, D5, D4, D3, D2, D1, D0}));
  COUNTER_4BIT counter_4bit_1 (.ENB(ENB_CNTR), .CLK(CLK), .RST(COUNTER_RESET), .CNT_OUT(counter_4bit_1_cnt_out));

  // Notes on the sheet:
  //   contents of rom_1 (hex, n*v repeats v):
  //   1804 44 244 1005 12*0 1804 104 1005 8*0 1000 4*0 1804 1c 284 1005 1000 11*0 1804 c04 1005 13*0 1804
  //   15*0 1804 1c 84 1005 12*0 1804 1c e084 f004 1005 11*0 1804 1c a084 b084 1005 11*0 1804 2004 1005
  //   13*0 1804 4006 1005 13*0 1804 2c a4 1005 28*0 1804 6006 1005 301*0 1804
endmodule

// RESISTER_8BIT
module UNIT_RESISTER (
  input  [7:0] IN_RES,
  input  WE_RES,
  input  CLK,
  input  RESET_DATA,
  output [7:0] DATA_OUT
);

  Register register_1 (.D(IN_RES), .en(WE_RES), .clk(CLK), .Q(DATA_OUT), .clr(RESET_DATA));
endmodule

// TAP7
module BIT_EXTRACTOR (
  input  [7:0] IN_07,
  output OUT_7,
  output [7:0] OUT_07
);


  assign OUT_07 = IN_07;
  assign OUT_7 = IN_07[7];
endmodule

// FLAG_GEN
module FLAG_GENERATOR (
  input  A7_IN,
  input  B7_IN,
  input  [7:0] RESULT_IN,
  input  [2:0] COMPARATOR_IN,
  output ARITH_OVERFLOW,
  output LSB_0_FLG,
  output ZERO_FLG,
  output NEG_LESS,
  output EQUAL_FLG
);

  wire and_1_out, and_2_out, not_2_out, not_3_out, not_4_out, or_1_out;

  or or_1 (or_1_out, RESULT_IN[0], RESULT_IN[1], RESULT_IN[2], RESULT_IN[3], RESULT_IN[4], RESULT_IN[5], RESULT_IN[6], RESULT_IN[7]);
  not not_1 (ZERO_FLG, or_1_out);
  and and_1 (and_1_out, A7_IN, B7_IN, not_2_out);
  not not_2 (not_2_out, RESULT_IN[7]);
  not not_3 (not_3_out, A7_IN);
  not not_4 (not_4_out, B7_IN);
  and and_2 (and_2_out, not_3_out, not_4_out, RESULT_IN[7]);
  or or_2 (NEG_LESS, RESULT_IN[7], COMPARATOR_IN[2]);
  or or_3 (ARITH_OVERFLOW, and_1_out, and_2_out);

  assign EQUAL_FLG = COMPARATOR_IN[1];
  assign LSB_0_FLG = RESULT_IN[0];
endmodule

module FLAG_RES (
  input  FI_R0,
  input  FI_R1,
  input  FI_R2,
  input  FI_R3,
  input  WE_FLAG,
  input  CLK,
  input  RESET_FLAG_RES,
  output FO_R0,
  output FO_R1,
  output FO_R2,
  output FO_R3
);

  Register #(.width(4)) register_1 (
    .D({FI_R3, FI_R2, FI_R1, FI_R0}), .en(WE_FLAG), .clk(CLK), .Q({FO_R3, FO_R2, FO_R1, FO_R0}),
    .clr(RESET_FLAG_RES));
endmodule

// GPR_ND_MUX
module MUXED_GP_RES (
  input  [7:0] DATA_IN,
  input  WE_T,
  input  [2:0] WE_SEL,
  input  CLEAR_ALL,
  input  CLK,
  input  [2:0] SEL_RES,
  output [7:0] DATA_OUT
);

  wire [7:0] gp_res_1_out_r0, gp_res_1_out_r1, gp_res_1_out_r2, gp_res_1_out_r3, gp_res_1_out_r4,
       gp_res_1_out_r5, gp_res_1_out_r6, gp_res_1_out_r7;

  GP_RES gp_res_1 (
    .WE_T(WE_T), .CLR_SEL(CLEAR_ALL), .CLK(CLK), .WE_SEL(WE_SEL), .IN_RES(DATA_IN), .OUT_R0(gp_res_1_out_r0),
    .OUT_R1(gp_res_1_out_r1), .OUT_R2(gp_res_1_out_r2), .OUT_R3(gp_res_1_out_r3), .OUT_R4(gp_res_1_out_r4),
    .OUT_R5(gp_res_1_out_r5), .OUT_R6(gp_res_1_out_r6), .OUT_R7(gp_res_1_out_r7));
  B_RESISTER_SELECTOR b_resister_selector_1 (
    .R0(gp_res_1_out_r0), .R1(gp_res_1_out_r1), .R2(gp_res_1_out_r2), .R3(gp_res_1_out_r3),
    .R4(gp_res_1_out_r4), .R5(gp_res_1_out_r5), .R6(gp_res_1_out_r6), .R7(gp_res_1_out_r7), .SEL_B(SEL_RES),
    .SELECTED_B(DATA_OUT));
endmodule

// FLG_REG
module FLG_RESISTER (
  input  FLG_0,
  input  FLG_1,
  input  FLG_2,
  input  FLG_3,
  input  FLG_4,
  input  WE_FLG,
  input  CLK,
  input  CLR_FLG,
  output FLG_O0,
  output FLG_O1,
  output FLG_O2,
  output FLG_O3,
  output FLG_O4
);

  Register #(.width(5)) register_1 (
    .D({FLG_4, FLG_3, FLG_2, FLG_1, FLG_0}), .en(WE_FLG), .clk(CLK),
    .Q({FLG_O4, FLG_O3, FLG_O2, FLG_O1, FLG_O0}), .clr(CLR_FLG));
endmodule

// PGRM_CNTR
module PROGRAM_COUNTER (
  input  [7:0] JMP_ADDR,
  input  JUMP_OTHERS,
  input  WE_PC,
  input  CLK,
  input  RESET,
  input  HALT,
  output [7:0] CURRENT_ADDR
);

  wire [0:0] nand_1_out;
  wire [7:0] adder_1_out, multiplexer_1_out;

  Multiplexer #(.width(8)) multiplexer_1 (
    .in0(adder_1_out), .in1(JMP_ADDR), .out(multiplexer_1_out), .sel(JUMP_OTHERS));
  Register register_1 (.D(multiplexer_1_out), .en(WE_PC), .clk(CLK), .Q(CURRENT_ADDR), .clr(RESET));
  nand nand_1 (nand_1_out[0], 1'b1, HALT);
  Adder adder_1 (.a(CURRENT_ADDR), .b({{7{1'b0}}, nand_1_out[0]}), .out(adder_1_out));  // open: cin, cout
endmodule

// PC_IR
module IR_PC (
);

  PROGRAM_COUNTER program_counter_1 ();  // open: JMP_ADDR, HALT, JUMP_OTHERS, WE_PC, CLK, RESET, CURRENT_ADDR
endmodule

// INST_DCDR
module INS_DECODER (
  input  [15:0] INSTRUCTION_INP,
  output [7:0] JUMP_ADDRESS,
  output [2:0] ALU_OP,
  output [7:0] DATA,
  output [2:0] SRC_B,
  output [2:0] DEST_RES,
  output [4:0] OPCODE,
  output HALT_OPCODE
);

  wire or_1_out;

  Demultiplexer #(.width(3)) demultiplexer_1 (
    .out0(DATA[7:5]), .out1(SRC_B), .in(INSTRUCTION_INP[7:5]), .sel(or_1_out));
  or or_1 (or_1_out, INSTRUCTION_INP[11], INSTRUCTION_INP[12], INSTRUCTION_INP[13], INSTRUCTION_INP[14], INSTRUCTION_INP[15]);
  and and_1 (HALT_OPCODE, INSTRUCTION_INP[11], INSTRUCTION_INP[12], INSTRUCTION_INP[13], INSTRUCTION_INP[14], INSTRUCTION_INP[15]);

  assign ALU_OP = INSTRUCTION_INP[2:0];
  assign DATA[4:0] = INSTRUCTION_INP[4:0];
  assign DEST_RES = INSTRUCTION_INP[10:8];
  assign JUMP_ADDRESS = INSTRUCTION_INP[7:0];
  assign OPCODE = INSTRUCTION_INP[15:11];
endmodule

// DISP_DRIVER
module DISPLAY_DRIVER (
  input  [7:0] DATA_IN,
  input  OVERFLOW,
  input  PRINT_ENB,
  input  RST,
  output SIGN_BIT,
  output ERROR,
  output [11:0] DISPLAY_PINS
);

  wire and_1_out, and_3_out, clock_1_out, not_1_out;
  wire [1:0] or_1_out;
  wire [11:0] multiplexer_1_out, rom_1_data;

  ROM #(.dataWidth(12)) rom_1 (.addr(DATA_IN), .data(rom_1_data));
  and and_1 (and_1_out, DATA_IN[7], PRINT_ENB);
  and and_2 (or_1_out[1], PRINT_ENB, OVERFLOW);
  and and_3 (and_3_out, and_1_out, not_1_out);
  not not_1 (not_1_out, or_1_out[1]);
  or or_1 (or_1_out[0], and_3_out, or_1_out[1]);
  Multiplexer #(.select(2), .width(12)) multiplexer_1 (
    .in1(rom_1_data), .in3(12'heee), .out(multiplexer_1_out), .sel({OVERFLOW, PRINT_ENB}));  // open: in0, in2
  Register #(.width(14)) register_1 (
    .D({multiplexer_1_out, or_1_out}), .en(PRINT_ENB), .clk(clock_1_out),
    .Q({DISPLAY_PINS, ERROR, SIGN_BIT}), .clr(RST));
  Clock clock_1 (.out(clock_1_out));

  // Notes on the sheet:
  //   contents of rom_1 (hex, n*v repeats v):
  //   0 1 2 3 4 5 6 7 8 9 10 11 12 13 14 15 16 17 18 19 20 21 22 23 24 25 26 27 28 29 30 31 32 33 34 35 36
  //   37 38 39 40 41 42 43 44 45 46 47 48 49 50 51 52 53 54 55 56 57 58 59 60 61 62 63 64 65 66 67 68 69
  //   70 71 72 73 74 75 76 77 78 79 80 81 82 83 84 85 86 87 88 89 90 91 92 93 94 95 96 97 98 99 100 101
  //   102 103 104 105 106 107 108 109 110 111 112 113 114 115 116 117 118 119 120 121 122 123 124 125 126
  //   127 128 127 126 125 124 123 122 121 120 119 118 117 116 115 114 113 112 111 110 109 108 107 106 105
  //   104 103 102 101 100 99 98 97 96 95 94 93 92 91 90 89 88 87 86 85 84 83 82 81 80 79 78 77 76 75 74 73
  //   72 71 70 69 68 67 66 65 64 63 62 61 60 59 58 57 56 55 54 53 52 51 50 49 48 47 46 45 44 43 42 41 40
  //   39 38 37 36 35 34 33 32 31 30 29 28 27 26 25 24 23 22 21 20 19 18 17 16 15 14 13 12 11 10 9 8 7 6 5
  //   4 3 2 1
endmodule

// JMP_DEC
module JUMP_LOGIC (
  input  [2:0] jump_logic_sel,
  input  t,
  input  [4:0] jump_flgs,
  output jump
);

  wire multiplexer_1_out, not_1_out, not_2_out;

  and and_1 (jump, t, multiplexer_1_out);
  not not_1 (not_1_out, jump_flgs[4]);
  Multiplexer #(.select(3)) multiplexer_1 (
    .in0(jump_flgs[0]), .in1(jump_flgs[1]), .in2(jump_flgs[2]), .in3(jump_flgs[3]), .in4(not_1_out),
    .in5(not_2_out), .in6(1'b1), .out(multiplexer_1_out), .sel(jump_logic_sel));  // open: in7
  not not_2 (not_2_out, jump_flgs[0]);
endmodule

module D_FLIP_FLOP (
  input  D,
  input  CLK,
  output out_3
);

  wire nand_1_out, nand_2_out, nand_4_out, not_1_out;

  not not_1 (not_1_out, D);
  nand nand_1 (nand_1_out, D, CLK);
  nand nand_2 (nand_2_out, CLK, not_1_out);
  nand nand_3 (out_3, nand_1_out, nand_4_out);
  nand nand_4 (nand_4_out, out_3, nand_2_out);
endmodule

module RESISTER_8BIT (
  input  in_1,
  input  [7:0] D,
  output [7:0] Q
);

  D_FLIP_FLOP d_flip_flop_1 (.D(D[0]), .CLK(in_1), .out_3(Q[0]));
  D_FLIP_FLOP d_flip_flop_2 (.D(D[1]), .CLK(in_1), .out_3(Q[1]));
  D_FLIP_FLOP d_flip_flop_3 (.D(D[2]), .CLK(in_1), .out_3(Q[2]));
  D_FLIP_FLOP d_flip_flop_4 (.D(D[3]), .CLK(in_1), .out_3(Q[3]));
  D_FLIP_FLOP d_flip_flop_5 (.D(D[4]), .CLK(in_1), .out_3(Q[4]));
  D_FLIP_FLOP d_flip_flop_6 (.D(D[5]), .CLK(in_1), .out_3(Q[5]));
  D_FLIP_FLOP d_flip_flop_7 (.D(D[6]), .CLK(in_1), .out_3(Q[6]));
  D_FLIP_FLOP d_flip_flop_8 (.D(D[7]), .CLK(in_1), .out_3(Q[7]));
endmodule

// UP_CNTR
module COUNTER_4BIT (
  input  ENB,
  input  CLK,
  input  RST,
  output [3:0] CNT_OUT
);

  wire not_1_out, not_2_out, not_3_out, not_4_out;

  Register #(.width(1)) register_1 (.D(not_1_out), .en(ENB), .clk(CLK), .Q(CNT_OUT[0]), .clr(RST));
  Register #(.width(1)) register_2 (.D(not_2_out), .en(ENB), .clk(not_1_out), .Q(CNT_OUT[1]), .clr(RST));
  not not_1 (not_1_out, CNT_OUT[0]);
  Register #(.width(1)) register_3 (.D(not_3_out), .en(ENB), .clk(not_2_out), .Q(CNT_OUT[2]), .clr(RST));
  not not_2 (not_2_out, CNT_OUT[1]);
  not not_3 (not_3_out, CNT_OUT[2]);
  not not_4 (not_4_out, CNT_OUT[3]);
  Register #(.width(1)) register_4 (.D(not_4_out), .en(ENB), .clk(not_3_out), .Q(CNT_OUT[3]), .clr(RST));
endmodule

// DCDR_3X8
module DEC_8X3 (
  input  I_0,
  input  I_1,
  input  I_2,
  input  I_3,
  input  I_4,
  input  I_5,
  input  I_6,
  input  I_7,
  input  [2:0] S,
  output out_10
);

  wire and_1_out, and_2_out, and_3_out, and_4_out, and_5_out, and_6_out, and_7_out, and_8_out, not_1_out,
       not_2_out, not_3_out;

  not not_1 (not_1_out, S[2]);
  not not_2 (not_2_out, S[1]);
  not not_3 (not_3_out, S[0]);
  and and_1 (and_1_out, I_0, not_1_out, not_2_out, not_3_out);
  and and_2 (and_2_out, I_1, not_1_out, not_2_out, S[0]);
  and and_3 (and_3_out, I_2, not_1_out, S[1], not_3_out);
  and and_4 (and_4_out, I_3, not_1_out, not_2_out, S[0]);
  and and_5 (and_5_out, I_4, S[2], S[1], not_3_out);
  and and_6 (and_6_out, I_5, S[2], not_2_out, S[0]);
  and and_7 (and_7_out, I_6, S[2], S[1], S[0]);
  and and_8 (and_8_out, I_7, S[2], S[1], S[0]);
  or or_1 (out_10, and_1_out, and_2_out, and_3_out, and_4_out, and_5_out, and_6_out, and_7_out, and_8_out);
endmodule
